# Fritzing sketch intro (saved by Fritzing 0.9.5d)
breadboards: 1

parts:
  Part1 = Arduino Nano (Rev3.0)
  LED1 = RGB LED (com. cathode, rgb) [package="5 mm [THT]"]
  R1 = Resistor [tolerance=±5% resistance=220 package=THT]

nets:
  N1: Part1.GND, Part1.D9, LED1.common_cathode
  N2: Part1.D10, Part1.A7
  N3: Part1.D11/MOSI, LED1.blue_anode
  N4: LED1.red_anode, R1.Pin_1
