# Fritzing sketch rtc_watch (saved by Fritzing 0.9.5d)
breadboards: 1

parts:
  Part1 = Arduino Nano (Rev3.0)
  Part2 = Adafruit DS3231 [part_number="Adafruit #3013"]
  U3 = Nokia 6100 Color LCD [package=nokia6100_lcd]

nets:
  GND: Part1.GND, Part2.GND, U3.VLED
  N1: Part1.A5, Part2.SCL, U3.GND
  N2: Part1.A4, Part2.SDA, U3.VDISPLAY
  3V3: Part1.3V3, Part2.Vin, U3.LEDGND

notes:
  This is not the screen we have.
  GND/VCC/SCL/SDA

custom parts:
  Adafruit DS3231: The datasheet for the DS3231 explains that this part is an "Extremely Accurate I²C-Integrated RTC/TCXO/Crystal". And, hey, it does exactly what it says on the tin! This Real Time Clock (RTC) is the most precise you can get in a small, low power package. Most RTCs use an external 32kHz timing crystal that is used to keep time with low current draw. And that's all well and good, but those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
