# Fritzing sketch buzzer (saved by Fritzing 0.9.5d)
breadboards: 1

parts:
  J1 = Piezo Speaker
  Part1 = Arduino Nano (Rev3.0)
  R1 = Resistor [tolerance=±5% resistance=100 package=THT]

nets:
  N1: J1.pin1, Part1.GND
  N2: J1.pin2, R1.Pin_1
  N3: Part1.D3, R1.Pin_0
