# Fritzing sketch buzzer (saved by Fritzing 0.9.5d)
breadboards: 1

parts:
  J2 = Piezo Speaker
  Part2 = Arduino Nano (Rev3.0)
  R2 = Resistor [tolerance=±5% resistance=100 package=THT]
  LED1 = RGB LED (com. cathode, rgb) [package="5 mm [THT]"]
  R3 = Resistor [tolerance=±5% resistance=470 package=THT]
  R4 = Resistor [tolerance=±5% resistance=470 package=THT]
  R5 = Resistor [tolerance=±5% resistance=470 package=THT]

nets:
  N1: J2.pin1, Part2.GND, LED1.common_cathode
  N2: J2.pin2, R2.Pin_1
  N3: Part2.D2, R2.Pin_0
  N4: Part2.D3, R3.Pin_1
  N5: Part2.D4, R4.Pin_1
  N6: Part2.D5, R5.Pin_1
  N7: LED1.red_anode, R3.Pin_0
  N8: LED1.green_anode, R4.Pin_0
  N9: LED1.blue_anode, R5.Pin_0
