# Fritzing sketch rgb_led (saved by Fritzing 0.9.5d)
breadboards: 1

parts:
  Part3 = Arduino Nano (Rev3.0)
  LED3 = RGB LED (com. cathode, rgb) [package="5 mm [THT]"]
  R7 = Resistor [tolerance=±5% resistance=470 package=THT]
  R8 = Resistor [tolerance=±5% resistance=470 package=THT]
  R9 = Resistor [tolerance=±5% resistance=470 package=THT]

nets:
  N1: Part3.GND, LED3.common_cathode
  N2: Part3.D3, R7.Pin_1
  N3: Part3.D4, R9.Pin_1
  N4: Part3.D5, R8.Pin_1
  N5: LED3.red_anode, R7.Pin_0
  N6: LED3.green_anode, R9.Pin_0
  N7: LED3.blue_anode, R8.Pin_0
