# Fritzing sketch office_buzzer (saved by Fritzing 0.9.5d)
breadboards: 1

parts:
  Part2 = Arduino Nano (Rev3.0)
  R2 = Resistor [tolerance=±5% resistance=100 package=THT]
  RE1 = Rotary Encoder [package=THT]
  J2 = Piezo Speaker

nets:
  N1: Part2.GND, J2.pin1
  N2: Part2.D4, R2.Pin_1
  N3: Part2.D5, RE1.EncoderPinA
  N4: Part2.D6, RE1.EncoderPinC
  N5: Part2.D7, RE1.EncoderPinB
  N6: R2.Pin_0, J2.pin2

notes:
  5-pin rotary encoder
