# Fritzing sketch music_game (saved by Fritzing 0.9.5d)
breadboards: 1

parts:
  Part2 = Arduino Nano (Rev3.0)
  LED2 = RGB LED (com. cathode, rgb) [package="5 mm [THT]"]
  R1 = Resistor [tolerance=±5% resistance=470 package=THT]
  R2 = Resistor [tolerance=±5% resistance=470 package=THT]
  R3 = Resistor [tolerance=±5% resistance=470 package=THT]
  S1 = Pushbutton [package="[THT]"]
  S2 = Pushbutton [package="[THT]"]
  S3 = Pushbutton [package="[THT]"]
  S4 = Pushbutton [package="[THT]"]
  R4 = Resistor [tolerance=±5% resistance=100 package=THT]
  J1 = Piezo Speaker

nets:
  N1: Part2.GND, Part2.D6, LED2.common_cathode, R3.Pin_1, S1.Pin_3, S1.Pin_4, S2.Pin_3, S2.Pin_4, S3.Pin_3, S3.Pin_4, S4.Pin_3, S4.Pin_4, J1.pin1
  N2: Part2.D2, S1.Pin_1, S1.Pin_2
  N3: Part2.D3, S2.Pin_1, S2.Pin_2
  N4: Part2.D4, S3.Pin_1, S3.Pin_2
  N5: Part2.D5, S4.Pin_1, S4.Pin_2
  N6: Part2.A3, R2.Pin_1
  N7: Part2.A2, R1.Pin_1
  N8: Part2.A1, R4.Pin_1
  N9: LED2.red_anode, R3.Pin_0
  N10: LED2.green_anode, R2.Pin_0
  N11: LED2.blue_anode, R1.Pin_0
  N12: R4.Pin_0, J1.pin2
