# Fritzing sketch push_button (saved by Fritzing 0.9.5d)
breadboards: 1

parts:
  Part2 = Arduino Nano (Rev3.0)
  R2 = Resistor [tolerance=±5% resistance=100 package=THT]
  J2 = Piezo Speaker
  S1 = Pushbutton [package="[THT]"]

nets (from the breadboard view):
  N1: Part2.GND, J2.pin1
  N2: Part2.3V3, S1.Pin_3, S1.Pin_4
  N3: R2.Pin_0, J2.pin2
  N4: R2.Pin_1, S1.Pin_1, S1.Pin_2
