# Fritzing sketch screen_example (saved by Fritzing 0.9.5d)
breadboards: 1

parts:
  U2 = Nokia 6100 Color LCD [package=nokia6100_lcd]
  Part1 = Arduino Nano (Rev3.0)

nets:
  N1: U2.VDISPLAY, Part1.A4
  N2: U2.GND, Part1.A5
  N3: U2.LEDGND, Part1.3V3
  N4: U2.VLED, Part1.GND

notes:
  This is not the screen we have.
  GND/VCC/SCL/SDA
