# Fritzing sketch speed_game (saved by Fritzing 0.9.5d)
breadboards: 1

parts:
  U2 = Nokia 6100 Color LCD [package=nokia6100_lcd]
  Part1 = Arduino Nano (Rev3.0)
  S1 = Pushbutton [package="[THT]"]
  S2 = Pushbutton [package="[THT]"]
  LED1 = RGB LED (com. cathode, rgb) [package="5 mm [THT]"]
  R1 = Resistor [tolerance=±5% resistance=470 package=THT]

nets:
  N1: U2.VDISPLAY, Part1.A4
  N2: U2.GND, Part1.A5
  N3: U2.LEDGND, Part1.3V3
  N4: U2.VLED, Part1.GND, S1.Pin_1, S1.Pin_2, S2.Pin_1, S2.Pin_2, LED1.common_cathode
  N5: Part1.D3, S1.Pin_3, S1.Pin_4
  N6: Part1.D4, S2.Pin_3, S2.Pin_4
  N7: Part1.D5, R1.Pin_1
  N8: LED1.red_anode, R1.Pin_0

notes:
  This is not the screen we have.
  GND/VCC/SCL/SDA
