# Fritzing sketch casio_clone (saved by Fritzing 0.9.5d)
breadboards: 1

parts:
  Part1 = Arduino Nano (Rev3.0)
  Part2 = Adafruit DS3231 [part_number="Adafruit #3013"]
  OLED1 = OLED 128x64 I2C Monochrome Display
  S1 = Pushbutton [package="[THT]"]
  S2 = Pushbutton [package="[THT]"]

nets:
  GND: Part1.GND, Part2.GND, OLED1.GND, S1.Pin_1, S1.Pin_2, S2.Pin_1, S2.Pin_2
  N1: Part1.D3, S2.Pin_3, S2.Pin_4
  N2: Part1.D4, Part2.!RTC_RST, S1.Pin_3, S1.Pin_4
  N3: Part1.A5, Part2.SCL, OLED1.SCK
  N4: Part1.A4, Part2.SDA, OLED1.SDA
  3V3: Part1.3V3, Part2.Vin, OLED1.VDD

custom parts:
  Adafruit DS3231: The datasheet for the DS3231 explains that this part is an "Extremely Accurate I²C-Integrated RTC/TCXO/Crystal". And, hey, it does exactly what it says on the tin! This Real Time Clock (RTC) is the most precise you can get in a small, low power package. Most RTCs use an external 32kHz timing crystal that is used to keep time with low current draw. And that's all well and good, but those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
